// Logisim project control_logic.circ as structural Verilog: 1 circuit, main circuit control_logic
module control_logic (
  input  [31:0] inst,
  input  BrEq,
  input  BrLt,
  output PCSel,
  output RegWEn,
  output [2:0] ImmSel,
  output BrUn,
  output ASel,
  output BSel,
  output [3:0] ALUSel,
  output MemRW,
  output [1:0] WBSel,
  output CSRSel,
  output CSRWen,
  output [4:0] rs1,
  output [4:0] rs2,
  output [4:0] rd
);

  wire [3:0] IaluSel, LorA, RaluSel;

  Multiplexer #(.enable("false"), .select(5), .width(4)) multiplexer_1 (
    .in0(4'b0000), .in1(4'b1010), .in2(4'b1100), .in4(4'b0110), .in5(4'b1110), .in8(4'b0111), .in13(4'b1011),
    .in16(4'b0011), .in20(4'b0100), .in22(4'b0101), .in24(4'b0010), .in28(4'b0001), .out(RaluSel),
    .sel({inst[14:12], inst[30], inst[25]}));  // open: in3, in6, in7, in9, in10, in11, in12, in14, in15, in17, in18, in19, in21, in23, in25, in26, in27, in29, in30, in31
  Multiplexer #(.enable("false"), .width(4)) multiplexer_2 (.in0(IaluSel), .in1(RaluSel), .out(ALUSel), .sel(inst[5]));
  Multiplexer #(.enable("false"), .width(4)) multiplexer_3 (.in0(4'b0100), .in1(4'b0101), .out(LorA), .sel(inst[30]));
  Multiplexer #(.enable("false"), .select(5), .width(3)) multiplexer_4 (
    .in0(3'b000), .in4(3'b000), .in5(3'b011), .in8(3'b001), .in13(3'b100), .in24(3'b010), .in25(3'b000),
    .in27(3'b101), .in28(3'b000), .out(ImmSel), .sel(inst[6:2]));  // open: in1, in2, in3, in6, in7, in9, in10, in11, in12, in14, in15, in16, in17, in18, in19, in20, in21, in22, in23, in26, in29, in30, in31
  Multiplexer #(.enable("false"), .select(3), .width(4)) multiplexer_5 (
    .in0(4'b0000), .in1(4'b0110), .in2(4'b0111), .in4(4'b0011), .in5(LorA), .in6(4'b0010), .in7(4'b0001),
    .out(IaluSel), .sel(inst[14:12]));  // open: in3

  assign BrUn = inst[13];
  assign BSel = inst[5];
  assign rd = inst[11:7];
  assign RegWEn = 1'b1;
  assign rs1 = inst[19:15];
  assign rs2 = inst[24:20];
  assign WBSel = 2'b00;

  // Other names for the same wires on the sheet: aluFun7[1:0] = {inst[30], inst[25]};
  //   aluFunc37[4:0] = {inst[14:12], inst[30], inst[25]}; func7imm[6:0] = inst[31:25];
  //   IaluFunc37[3:0] = {inst[14:12], inst[30]}; LorASel = inst[30]; func3[2:0] = inst[14:12]; sign = inst[14];
  //   opcode[6:0] = inst[6:0]

  // Notes on the sheet:
  //   ALUSelDesjgn
  //   INPUTS to your circuit
  //   DON'T CHANGE THE LOCATIONS OF THE INPUTS AND OUTPUTS!
  //   OUTPUT from your circuit
endmodule
