// Logisim project cpu.circ as structural Verilog: 1 circuit, main circuit cpu
module cpu (
  input  clk,
  input  [31:0] INSTRUCTION,
  input  [31:0] READ_DATA,
  output [31:0] WRITE_ADDRESS,
  output [31:0] PROGRAM_COUNTER,
  output [31:0] ra,
  output [31:0] sp,
  output [31:0] t0,
  output [31:0] t1,
  output [31:0] t2,
  output [31:0] s0,
  output [31:0] s1,
  output [31:0] a0,
  output [31:0] tohost,
  output [3:0] WRITE_ENABLE,
  output [31:0] WRITE_DATA
);

  wire BrEq, BrLt, BrUn, BSel, MemRW, RegWEn;
  wire [1:0] WBSel;
  wire [2:0] ImmSel;
  wire [3:0] ALUSel;
  wire [4:0] rd, rs1, rs2;
  wire [31:0] adder_1_out, aluResult, B, immediate, INSTRUCTION1, loadREAD_DATA, Read_Data_1, Read_Data_2,
       Write_Data_t;

  Adder #(.width(32)) adder_1 (.a(PROGRAM_COUNTER), .b(32'h4), .out(adder_1_out));  // open: cin, cout
  Register #(.width(32)) PC (.D(adder_1_out), .clk(clk), .Q(PROGRAM_COUNTER));  // open: en, clr
  Register #(.width(32)) register_1 (.D(INSTRUCTION), .clk(clk), .Q(INSTRUCTION1));  // open: en, clr
  Multiplexer #(.enable("false"), .width(32)) multiplexer_1 (.in0(immediate), .in1(Read_Data_2), .out(B), .sel(BSel));
  Adder #(.width(32)) adder_2 (.a(Read_Data_1), .b(immediate), .out(WRITE_ADDRESS));  // open: cin, cout
  control_logic control_logic_1 (
    .rs1(rs1), .rs2(rs2), .rd(rd), .WRITE_ENABLE(WRITE_ENABLE), .load_read_data(loadREAD_DATA),
    .SwriteData(WRITE_DATA), .RegWEn(RegWEn), .ImmSel(ImmSel), .BrUn(BrUn), .BSel(BSel), .ALUSel(ALUSel),
    .MemRW(MemRW), .WBSel(WBSel), .inst(INSTRUCTION1), .MEM_READ_DATA(READ_DATA),
    .bytePos(WRITE_ADDRESS[1:0]), .Reg2Data(Read_Data_2), .BrEq(BrEq), .BrLt(BrLt));  // open: CSRWen, PCSel, ASel, CSRSel
  imm_gen imm_gen_1 (.inst(INSTRUCTION1), .ImmSel(ImmSel), .imm(immediate));
  regfile regfile_1 (
    .rs1(rs1), .rs2(rs2), .rd(rd), .Write_Data(Write_Data_t), .RegWEn(RegWEn), .clk(clk), .ra(ra), .sp(sp),
    .t0(t0), .t1(t1), .t2(t2), .s0(s0), .s1(s1), .a0(a0), .Read_Data_1(Read_Data_1), .Read_Data_2(Read_Data_2));
  branch_comp branch_comp_1 (.rs1(Read_Data_1), .rs2(Read_Data_2), .BrUn(BrUn), .BrEq(BrEq), .BrLt(BrLt));
  alu alu_1 (.Result(aluResult), .A(Read_Data_1), .B(B), .ALUSel(ALUSel));
  csr csr_1 (.tohost(tohost));  // open: CSR_address, CSR_din, CSR_WE, clk
  Multiplexer #(.enable("false"), .select(2), .width(32)) multiplexer_2 (
    .in0(aluResult), .in1(loadREAD_DATA), .out(Write_Data_t), .sel(WBSel));  // open: in2, in3

  // Other names for the same wires on the sheet: bytePos[1:0] = WRITE_ADDRESS[1:0]

  // Notes on the sheet:
  //   Output to IMEM
  //   IMEM (do **NOT** move this)
  //   Inputs from IMEM
  //   It is OK to move the PC, RegFile, ALU, MEM, Branch Comp, Imm Gen, and Control Logic to wherever is most convenient for you when constructing your CPU, and to delete this text
  //   Inputs/Outputs for testing. Do **NOT** move these.
  //   Outputs To DMEM
  //   DMEM (do **NOT** move this)
  //   Inputs From DMEM
endmodule
